# Fritzing sketch scematic (saved by Fritzing 0.9.3b)
breadboards: 1

parts:
  BAT1_9V = BC9VPC [package=bc9vpc]
  BAT2_9V = BC9VPC [package=bc9vpc]
  Buck_Converter = RioRand LM2596
  Voltmeter_1 = Digital Panel Meter, Voltage, DMS-20PC
  Voltmeter_2 = Digital Panel Meter, Voltage, DMS-20PC
  S1 = Toggle Switch [package=THT]  # not connected
  DC_Female_Plug = Screw terminal - 2 pins [package=THT]

nets:
  N1: BAT1_9V.V-, BAT2_9V.V+
  N2: BAT2_9V.V-, Voltmeter_1.3:_GND
  N3: Buck_Converter.Pin_3, Voltmeter_2.1:_VCC, Voltmeter_2.11:_(+)_INPUT_HI, DC_Female_Plug.pin1
  N4: Buck_Converter.Pin_4, Voltmeter_2.3:_GND, DC_Female_Plug.pin2
